// Logisim project domaci2.circ as structural Verilog: 2 circuits, main circuit 1.
module _1 (
  input  x1,
  input  x2,
  input  x3,
  input  x4,
  input  x5,
  output y
);

  wire nor_1_out, nor_2_out, nor_3_out, nor_4_out, nor_5_out, nor_6_out, nor_7_out, nor_8_out, nor_9_out,
       nor_10_out, nor_11_out, nor_12_out, nor_13_out, nor_14_out;

  nor nor_1 (nor_1_out, x1, x1);
  nor nor_2 (nor_2_out, x4, x4);
  nor nor_3 (nor_3_out, x5, x5);
  nor nor_4 (nor_4_out, nor_1_out, nor_1_out);
  nor nor_5 (nor_5_out, x2, x2);
  nor nor_6 (nor_6_out, nor_2_out, nor_2_out);
  nor nor_7 (nor_7_out, nor_3_out, nor_3_out);
  nor nor_8 (nor_8_out, nor_4_out, nor_5_out);
  nor nor_9 (nor_9_out, nor_8_out, nor_8_out);
  nor nor_10 (nor_10_out, x3, x3);
  nor nor_11 (nor_11_out, nor_6_out, nor_7_out);
  nor nor_12 (nor_12_out, nor_9_out, nor_10_out);
  nor nor_13 (nor_13_out, nor_12_out, nor_12_out);
  nor nor_14 (nor_14_out, nor_11_out, nor_11_out);
  nor nor_15 (y, nor_13_out, nor_14_out);

  // Notes on the sheet:
  //   23.07
  //   2+3+7=12
  //   12-->
  //   01100
endmodule

module _2 (
  input  x1,
  input  x2,
  input  x3,
  input  x4,
  input  x5,
  output y
);

  wire nor_1_out, nor_2_out, nor_3_out, nor_4_out, nor_5_out, nor_6_out, nor_7_out, nor_8_out;

  nor nor_1 (nor_1_out, x2, x2);
  nor nor_2 (nor_2_out, x4, x5);
  nor nor_3 (nor_3_out, x1, nor_1_out);
  nor nor_4 (nor_4_out, nor_3_out, nor_3_out);
  nor nor_5 (nor_5_out, x3, x3);
  nor nor_6 (nor_6_out, nor_4_out, nor_5_out);
  nor nor_7 (nor_7_out, nor_6_out, nor_6_out);
  nor nor_8 (nor_8_out, nor_2_out, nor_2_out);
  nor nor_9 (y, nor_7_out, nor_8_out);
endmodule
